// Logisim project projectX (1).circ as structural Verilog
module _1_bit_ALU (
  input  A,
  input  B,
  input  [2:0] in_3,
  input  Cin,
  output Result,
  output Cout
);

  wire adder_1_out, and_1_out, and_2_out, multiplexer_1_out, nand_1_out, nor_1_out, not_1_out, or_1_out;

  Multiplexer #(.enable("false")) multiplexer_1 (.in0(B), .in1(not_1_out), .out(multiplexer_1_out), .sel(and_2_out));
  not not_1 (not_1_out, B);
  and and_1 (and_1_out, A, B);
  or or_1 (or_1_out, A, B);
  nand nand_1 (nand_1_out, A, B);
  nor nor_1 (nor_1_out, A, B);
  Adder #(.width(1)) adder_1 (.a(A), .b(multiplexer_1_out), .out(adder_1_out), .cin(Cin), .cout(Cout));
  and and_2 (and_2_out, in_3[0], in_3[2]);
  Multiplexer #(.select(3), .enable("false")) multiplexer_2 (
    .in0(and_1_out), .in1(or_1_out), .in2(nand_1_out), .in3(nor_1_out), .in4(adder_1_out), .in5(adder_1_out),
    .out(Result), .sel(in_3));  // open: in6, in7

  // Notes on the sheet:
  //   Figure: 1-bit ALU
endmodule

module Resigter_File (
  input  [9:0] Write_Data,
  input  Write_Register,
  input  [3:0] Read_Register_1,
  input  Clock_Pulse,
  input  [3:0] Write_Register_2,
  input  [3:0] Read_Register_2,
  output [9:0] Read_Data_1,
  output [9:0] Read_Data_2
);

  wire _0_out, _1_out, _2_out, _3_out, _4_out, _5_out, _6_out, _7_out, _8_out, _9_out, decoder_1_out0,
       decoder_1_out1, decoder_1_out2, decoder_1_out3, decoder_1_out4, decoder_1_out5, decoder_1_out6,
       decoder_1_out7, decoder_1_out8, decoder_1_out9;
  wire [9:0] R0_q, R1_q, R2_q, R3_q, R4_q, R5_q, R6_q, R7_q, R8_q, R9_q;

  Decoder #(.select(4), .enable("false")) decoder_1 (
    .out0(decoder_1_out0), .out1(decoder_1_out1), .out2(decoder_1_out2), .out3(decoder_1_out3),
    .out4(decoder_1_out4), .out5(decoder_1_out5), .out6(decoder_1_out6), .out7(decoder_1_out7),
    .out8(decoder_1_out8), .out9(decoder_1_out9), .sel(Write_Register_2));  // open: out10, out11, out12, out13, out14, out15
  and _1 (_1_out, decoder_1_out1, Write_Register);
  and _3 (_3_out, decoder_1_out3, Write_Register);
  and _5 (_5_out, decoder_1_out5, Write_Register);
  and _7 (_7_out, decoder_1_out7, Write_Register);
  and _9 (_9_out, decoder_1_out9, Write_Register);
  and _0 (_0_out, decoder_1_out0, Write_Register);
  and _2 (_2_out, decoder_1_out2, Write_Register);
  and _4 (_4_out, decoder_1_out4, Write_Register);
  and _6 (_6_out, decoder_1_out6, Write_Register);
  and _8 (_8_out, decoder_1_out8, Write_Register);
  Register #(.width(10)) R0 (.D(Write_Data), .en(_0_out), .Q(R0_q), .clk(Clock_Pulse));  // open: clr
  Register #(.width(10)) R2 (.D(Write_Data), .en(_2_out), .Q(R2_q), .clk(Clock_Pulse));  // open: clr
  Register #(.width(10)) R4 (.D(Write_Data), .en(_4_out), .Q(R4_q), .clk(Clock_Pulse));  // open: clr
  Register #(.width(10)) R6 (.D(Write_Data), .en(_6_out), .Q(R6_q), .clk(Clock_Pulse));  // open: clr
  Register #(.width(10)) R8 (.D(Write_Data), .en(_8_out), .Q(R8_q), .clk(Clock_Pulse));  // open: clr
  Register #(.width(10)) R1 (.D(Write_Data), .en(_1_out), .Q(R1_q), .clk(Clock_Pulse));  // open: clr
  Register #(.width(10)) R3 (.D(Write_Data), .en(_3_out), .Q(R3_q), .clk(Clock_Pulse));  // open: clr
  Register #(.width(10)) R5 (.D(Write_Data), .en(_5_out), .Q(R5_q), .clk(Clock_Pulse));  // open: clr
  Register #(.width(10)) R7 (.D(Write_Data), .en(_7_out), .Q(R7_q), .clk(Clock_Pulse));  // open: clr
  Register #(.width(10)) R9 (.D(Write_Data), .en(_9_out), .Q(R9_q), .clk(Clock_Pulse));  // open: clr
  Multiplexer #(.select(4), .width(10), .enable("false")) multiplexer_1 (
    .in0(R0_q), .in1(R1_q), .in2(R2_q), .in3(R3_q), .in4(R4_q), .in5(R5_q), .in6(R6_q), .in7(R7_q),
    .in8(R8_q), .in9(R9_q), .out(Read_Data_1), .sel(Read_Register_1));  // open: in10, in11, in12, in13, in14, in15
  Multiplexer #(.select(4), .width(10), .enable("false")) multiplexer_2 (
    .in0(R0_q), .in1(R1_q), .in2(R2_q), .in3(R3_q), .in4(R4_q), .in5(R5_q), .in6(R6_q), .in7(R7_q),
    .in8(R8_q), .in9(R9_q), .out(Read_Data_2), .sel(Read_Register_2));  // open: in10, in11, in12, in13, in14, in15
endmodule

module _10_bit_ALU (
  input  [2:0] Selection_Bit,
  input  Cin,
  input  [9:0] A,
  input  [9:0] B,
  output Cout,
  output [9:0] Result
);

  wire n1_bit_alu_1_cout, n1_bit_alu_2_cout, n1_bit_alu_3_cout, n1_bit_alu_4_cout, n1_bit_alu_5_cout,
       n1_bit_alu_6_cout, n1_bit_alu_7_cout, n1_bit_alu_9_cout, n1_bit_alu_10_cout;

  _1_bit_ALU u_1_bit_alu_1 (
    .A(A[0]), .B(B[0]), .Cin(Cin), .Result(Result[0]), .Cout(n1_bit_alu_1_cout), .in_3(Selection_Bit));
  _1_bit_ALU u_1_bit_alu_2 (
    .A(A[1]), .B(B[1]), .Cin(n1_bit_alu_1_cout), .Result(Result[1]), .Cout(n1_bit_alu_2_cout),
    .in_3(Selection_Bit));
  _1_bit_ALU u_1_bit_alu_3 (
    .A(A[2]), .B(B[2]), .Cin(n1_bit_alu_2_cout), .Result(Result[2]), .Cout(n1_bit_alu_3_cout),
    .in_3(Selection_Bit));
  _1_bit_ALU u_1_bit_alu_4 (
    .A(A[3]), .B(B[3]), .Cin(n1_bit_alu_3_cout), .Result(Result[3]), .Cout(n1_bit_alu_4_cout),
    .in_3(Selection_Bit));
  _1_bit_ALU u_1_bit_alu_5 (
    .A(A[4]), .B(B[4]), .Cin(n1_bit_alu_4_cout), .Result(Result[4]), .Cout(n1_bit_alu_5_cout),
    .in_3(Selection_Bit));
  _1_bit_ALU u_1_bit_alu_6 (
    .A(A[5]), .B(B[5]), .Cin(n1_bit_alu_5_cout), .Result(Result[5]), .Cout(n1_bit_alu_6_cout),
    .in_3(Selection_Bit));
  _1_bit_ALU u_1_bit_alu_7 (
    .A(A[7]), .B(B[7]), .Cin(n1_bit_alu_9_cout), .Result(Result[7]), .Cout(n1_bit_alu_7_cout),
    .in_3(Selection_Bit));
  _1_bit_ALU u_1_bit_alu_8 (
    .A(B[9]), .B(A[9]), .Cin(n1_bit_alu_10_cout), .Result(Result[9]), .Cout(Cout), .in_3(Selection_Bit));
  _1_bit_ALU u_1_bit_alu_9 (
    .A(A[6]), .B(B[6]), .Cin(n1_bit_alu_6_cout), .Result(Result[6]), .Cout(n1_bit_alu_9_cout),
    .in_3(Selection_Bit));
  _1_bit_ALU u_1_bit_alu_10 (
    .A(A[8]), .B(B[8]), .Cin(n1_bit_alu_7_cout), .Result(Result[8]), .Cout(n1_bit_alu_10_cout),
    .in_3(Selection_Bit));
endmodule

module Instruction_Fetch_Unit (
  input  Enable,
  input  Clear,
  input  Clock,
  output [9:0] out_4
);

  wire [9:0] adder_1_out, register_1_q;

  Register #(.width(10)) register_1 (.D(adder_1_out), .en(Enable), .Q(register_1_q), .clk(Clock), .clr(Clear));
  Adder #(.width(10)) adder_1 (.a(10'h1), .b(register_1_q), .out(adder_1_out));  // open: cin, cout
  ROM #(.addrWidth(10), .dataWidth(10)) rom_1 (.addr(register_1_q), .data(out_4));  // open: sel

  // Notes on the sheet:
  //   Figure: Instruction Fetch Unit
  //   contents of rom_1 (hex, n*v repeats v):
  //   162 f4 38
endmodule

module R_Type_Data_Path (
  input  Cin,
  input  [2:0] Opp,
  input  in_3,
  input  in_4,
  output out_5,
  output [2:0] out_6,
  output [9:0] out_7,
  output [9:0] out_8,
  output [9:0] out_9
);

  wire clock_1_out;
  wire [3:0] bit_extender_1_out, bit_extender_2_out;
  wire [6:0] instruction_fetch_unit_1_out_4;

  Instruction_Fetch_Unit instruction_fetch_unit_1 (
    .out_4({out_6, instruction_fetch_unit_1_out_4}), .Clear(in_4), .Clock(clock_1_out));  // open: Enable
  Clock clock_1 (.out(clock_1_out));
  assign bit_extender_1_out = {{2{1'b0}}, instruction_fetch_unit_1_out_4[6:5]};  // Bit_Extender bit_extender_1
  assign bit_extender_2_out = {{3{1'b0}}, instruction_fetch_unit_1_out_4[4]};  // Bit_Extender bit_extender_2
  Resigter_File resigter_file_1 (
    .Read_Data_1(out_7), .Read_Register_1(bit_extender_1_out), .Read_Data_2(out_8),
    .Read_Register_2(bit_extender_2_out), .Write_Register(in_3), .Write_Data(out_9),
    .Write_Register_2(instruction_fetch_unit_1_out_4[3:0]), .Clock_Pulse(clock_1_out));
  _10_bit_ALU u_10_bit_alu_1 (.Result(out_9), .A(out_7), .B(out_8), .Selection_Bit(Opp), .Cin(Cin), .Cout(out_5));
endmodule

module I_type_Datapath (
  input  Cin,
  input  [2:0] Opp,
  input  Enable,
  input  in_4,
  input  in_5,
  input  Str,
  input  load,
  input  Clear,
  output out_9,
  output [2:0] Opp_2,
  output [9:0] out_11,
  output [1:0] rs,
  output [9:0] RD1,
  output rt,
  output [9:0] RD2,
  output [3:0] rd,
  output [9:0] Result
);

  wire clock_1_out;
  wire [3:0] bit_extender_1_out, bit_extender_2_out;
  wire [9:0] bit_extender_3_out;

  Instruction_Fetch_Unit instruction_fetch_unit_1 (
    .out_4({Opp_2, rs, rt, rd}), .Clear(in_5), .Clock(clock_1_out), .Enable(Enable));
  Clock clock_1 (.out(clock_1_out));
  assign bit_extender_1_out = {{2{1'b0}}, rs};  // Bit_Extender bit_extender_1
  assign bit_extender_2_out = {{3{1'b0}}, rt};  // Bit_Extender bit_extender_2
  assign bit_extender_3_out = {{6{1'b0}}, rd};  // Bit_Extender bit_extender_3
  Resigter_File resigter_file_1 (
    .Read_Data_1(RD1), .Read_Register_1(bit_extender_1_out), .Read_Data_2(RD2),
    .Read_Register_2(bit_extender_2_out), .Write_Register(in_4), .Write_Data(out_11),
    .Write_Register_2(bit_extender_1_out), .Clock_Pulse(clock_1_out));
  _10_bit_ALU u_10_bit_alu_1 (
    .Result(Result), .A(RD1), .B(bit_extender_3_out), .Selection_Bit(Opp), .Cin(Cin), .Cout(out_9));
  RAM #(.addrWidth(10), .dataWidth(10), .bus("separate")) ram_1 (
    .addr(RD2), .din(Result), .data(out_11), .str(Str), .clk(clock_1_out), .ld(load), .clr(Clear));  // open: sel
endmodule

module Pipeline (
  input  Cin,
  input  [2:0] Opp,
  input  Enable,
  input  in_4,
  input  R_I,
  input  Mem_Res,
  input  in_7,
  input  R_I_2,
  input  Str,
  input  load,
  input  Clear,
  output out_12,
  output [9:0] RD1,
  output [9:0] RD2,
  output [3:0] Opp_2,
  output [9:0] Result,
  output [1:0] rs,
  output [1:0] rt,
  output [1:0] rd
);

  wire clock_1_out;
  wire [1:0] multiplexer_1_out;
  wire [3:0] bit_extender_1_out, bit_extender_2_out, bit_extender_3_out, bit_extender_4_out,
       bit_extender_7_out;
  wire [9:0] bit_extender_5_out, bit_extender_6_out, instruction_fetch_unit_1_out_4, multiplexer_2_out,
       multiplexer_3_out, n10_bit_alu_1_result, ram_1_data, register_2_q, register_3_q, register_4_q,
       register_5_q, register_7_q, register_8_q, register_10_q, register_11_q, resigter_file_1_read_data_2;

  Instruction_Fetch_Unit instruction_fetch_unit_1 (
    .out_4(instruction_fetch_unit_1_out_4), .Clear(in_7), .Clock(clock_1_out), .Enable(Enable));
  Clock clock_1 (.out(clock_1_out));
  Register #(.width(10)) register_1 (
    .D(instruction_fetch_unit_1_out_4), .Q({Opp_2, rs, rt, rd}), .clk(clock_1_out), .clr(in_7));  // open: en
  assign bit_extender_1_out = {{2{1'b0}}, rs};  // Bit_Extender bit_extender_1
  assign bit_extender_2_out = {{2{1'b0}}, rt};  // Bit_Extender bit_extender_2
  assign bit_extender_3_out = {{2{1'b0}}, rd};  // Bit_Extender bit_extender_3
  assign bit_extender_4_out = {{2{1'b0}}, multiplexer_1_out};  // Bit_Extender bit_extender_4
  Multiplexer #(.width(2), .enable("false")) multiplexer_1 (.in0(rd), .in1(rt), .out(multiplexer_1_out), .sel(R_I_2));
  assign bit_extender_5_out = {{6{1'b0}}, bit_extender_4_out};  // Bit_Extender bit_extender_5
  Resigter_File resigter_file_1 (
    .Read_Data_1(RD1), .Read_Register_1(bit_extender_1_out), .Read_Data_2(resigter_file_1_read_data_2),
    .Read_Register_2(bit_extender_2_out), .Write_Register(in_4), .Write_Data(multiplexer_3_out),
    .Write_Register_2(bit_extender_7_out), .Clock_Pulse(clock_1_out));
  assign bit_extender_6_out = {{6{1'b0}}, bit_extender_3_out};  // Bit_Extender bit_extender_6
  Register #(.width(10)) register_2 (
    .D(bit_extender_6_out), .Q(register_2_q), .clk(clock_1_out), .clr(in_7));  // open: en
  Register #(.width(10)) register_3 (
    .D(bit_extender_5_out), .Q(register_3_q), .clk(clock_1_out), .clr(in_7));  // open: en
  Multiplexer #(.width(10), .enable("false")) multiplexer_2 (
    .in0(resigter_file_1_read_data_2), .in1(register_2_q), .out(multiplexer_2_out), .sel(R_I));
  Register #(.width(10)) register_4 (.D(RD1), .Q(register_4_q), .clk(clock_1_out), .clr(in_7));  // open: en
  Register #(.width(10)) register_5 (
    .D(multiplexer_2_out), .Q(register_5_q), .clk(clock_1_out), .clr(in_7));  // open: en
  Register #(.width(10)) register_6 (
    .D(resigter_file_1_read_data_2), .Q(RD2), .clk(clock_1_out), .clr(in_7));  // open: en
  Register #(.width(10)) register_7 (.D(register_3_q), .Q(register_7_q), .clk(clock_1_out), .clr(in_7));  // open: en
  _10_bit_ALU u_10_bit_alu_1 (
    .Result(n10_bit_alu_1_result), .A(register_4_q), .B(register_5_q), .Selection_Bit(Opp), .Cin(Cin),
    .Cout(out_12));
  Register #(.width(10)) register_8 (.D(register_7_q), .Q(register_8_q), .clk(clock_1_out), .clr(in_7));  // open: en
  Bit_Extender #(.in_width(10), .out_width(4)) bit_extender_7 (.in(register_8_q), .out(bit_extender_7_out));
  Register #(.width(10)) register_9 (.D(n10_bit_alu_1_result), .Q(Result), .clk(clock_1_out), .clr(in_7));  // open: en
  Register #(.width(10)) register_10 (.D(RD2), .Q(register_10_q), .clk(clock_1_out), .clr(in_7));  // open: en
  RAM #(.addrWidth(10), .dataWidth(10), .bus("separate")) ram_1 (
    .addr(RD2), .din(Result), .data(ram_1_data), .str(Str), .clk(clock_1_out), .ld(load), .clr(Clear));  // open: sel
  Register #(.width(10)) register_11 (.D(ram_1_data), .Q(register_11_q), .clk(clock_1_out), .clr(in_7));  // open: en
  Multiplexer #(.width(10), .enable("false")) multiplexer_3 (
    .in0(register_10_q), .in1(register_11_q), .out(multiplexer_3_out), .sel(Mem_Res));
endmodule
